# Fritzing sketch Keyboard_PCBless (saved by Fritzing 0.9.9b)
breadboards: 1

parts:
  R1 = Resistor [tolerance=±5% power=0.25 resistance=10k package=THT]
  JP1 = Header 1 [package=1x01_offset]
  JP2 = Header 1 [package=1x01_offset]
  R2 = Short 10KΩ Resistor [package=THT]
  R3 = Short 10KΩ Resistor [package=THT]
  R4 = Short 10KΩ Resistor [package=THT]
  S1 = Pushbutton [package="[THT]"]
  S2 = Pushbutton [package="[THT]"]
  S3 = Pushbutton [package="[THT]"]
  S4 = Pushbutton [package="[THT]"]
  S5 = Pushbutton [package="[THT]"]
  R5 = Short 10KΩ Resistor [package=THT]

nets:
  N1: R1.Pin_0, JP2.1
  N2: R1.Pin_1, R2.Pin_1, S5.Pin_3, S5.Pin_4
  N3: JP1.1, S1.Pin_1, S1.Pin_2, S2.Pin_1, S2.Pin_2, S3.Pin_1, S3.Pin_2, S4.Pin_1, S4.Pin_2, S5.Pin_1, S5.Pin_2
  N4: R2.Pin_0, R3.Pin_1, S4.Pin_3, S4.Pin_4
  N5: R3.Pin_0, R4.Pin_1, S3.Pin_3, S3.Pin_4
  N6: R4.Pin_0, S2.Pin_3, S2.Pin_4, R5.Pin_1
  N7: S1.Pin_3, S1.Pin_4, R5.Pin_0

custom parts:
  Short 10KΩ Resistor: A generic resistor (0.25W) - short leads
