# Fritzing sketch Wireless_Joystick_Keyboard (saved by Fritzing 0.9.9b)
breadboards: 1

parts:
  Arduino_Nano = Arduino Nano (Rev3.0)
  R2 = Resistor [tolerance=±5% power=0.25 resistance=18k package=THT]
  R1 = Resistor [tolerance=±5% power=0.25 resistance=10k package=THT]
  Analog_Joystick = Thumb Joystick
  HM-10 = Bluetooth HM-10

nets:
  N1: Arduino_Nano.D1/TX, R1.Pin_0
  N2: Arduino_Nano.D0/RX, HM-10.TXD
  GND: Arduino_Nano.GND, R2.Pin_0, Analog_Joystick.GND, HM-10.GND
  N3: Arduino_Nano.D2, Analog_Joystick.SEL
  VCC: Arduino_Nano.5V, Analog_Joystick.VCC, HM-10.VCC
  N4: Arduino_Nano.A3, Analog_Joystick.VERT
  N5: Arduino_Nano.A2, Analog_Joystick.HORZ
  N6: R2.Pin_1, R1.Pin_1, HM-10.RXD
